# Fritzing sketch Practica2_Led.fz (saved by Fritzing 0.9.3b)
breadboards: 2

parts:
  C1 = Electrolytic Capacitor [capacitance=10µF voltage=50V package="100 mil [THT, electrolytic]"]
  LED1 = LED - 5mm [color="Red (633nm)" current=0.030A package="5 mm [THT]"]
  M1 = NRF24L01+ PA/LNA [package=THT]
  A1 = ESP32-S3-WROOM-1-N16R8 dev board
  M2 = DOIT Esp32 DevKit v1 (30 pins long, 11 pins width) [part_number=ESP32S-PIN30]
  M3 = NRF24L01+ PA/LNA [package=THT]
  C2 = Electrolytic Capacitor [capacitance=10µF voltage=50V package="100 mil [THT, electrolytic]"]
  LED2 = LED - 5mm [color="Green (555nm)" current=0.030A package="5 mm [THT]"]
  S1 = Pushbutton [package="[THT]"]
  R1 = Resistor [tolerance=±5% resistance=1k package=THT]
  LED3 = LED - 5mm [color="Red (633nm)" package="5 mm [THT]"]
  R2 = Resistor [tolerance=±5% resistance=220 package=THT]

nets:
  N1: C1.-, LED1.cathode, M1.GND, A1.Pin_22, A1.Pin_23, A1.Pin_24, A1.Pin_44
  N2: C1.+, LED1.anode, M1.VCC, A1.Pin_1, A1.Pin_2, S1.Pin_3, S1.Pin_4, R1.Pin_1
  N3: M1.MISO, A1.Pin_19
  N4: M1.MOSI, A1.Pin_17
  N5: M1.SCK, A1.Pin_18
  N6: M1.CSN, A1.Pin_5
  N7: M1.CE, A1.Pin_6
  N8: A1.Pin_41, S1.Pin_1, S1.Pin_2, R1.Pin_0
  3V3: M2.3V3, M3.VCC, C2.+, LED2.anode
  GND: M2.GND, M3.GND, C2.-, LED2.cathode, R2.Pin_1
  N9: M2.D2, M3.CE
  N10: M2.D5, M3.CSN
  N11: M2.D18, M3.SCK
  N12: M2.D19, M3.MISO
  N13: M2.D23, M3.MOSI
  N14: M2.D12, LED3.anode
  N15: LED3.cathode, R2.Pin_0

custom parts:
  NRF24L01+ PA/LNA: NRF24L01+ PA LNA Wireless Transceiver Module
  ESP32-S3-WROOM-1-N16R8 dev board: ESP32-S3 WIFI+BLE5.0 Development Board ESP32-S3-WROOM-1-N16R8(16M Flash/8SRAM).
  DOIT Esp32 DevKit v1 (30 pins long, 11 pins width): The DOIT Esp32 DevKit v1 is one of the development board created by DOIT to evaluate the ESP-WROOM-32 module. It is based on the ESP32 microcontroller that boasts Wifi, Bluetooth, Ethernet and Low Power support all in a single chip. (vanepp) made breadboard work, adjusted pin numbering and labels and reduced size of schematic and cleaned up pcb. This chip is 30pins long (2 x15) and 11 pins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
